// Logisim project latches.circ as structural Verilog: 8 circuits, main circuit NOR SR Latch
module NOR_SR_Latch (
  input  Set,
  input  Reset,
  output Q,
  output Q_prime
);

  nor nor_1 (Q, Set, Q_prime);
  nor nor_2 (Q_prime, Q, Reset);
endmodule

module NAND_SR_Latch (
  input  Set,
  input  Reset,
  output out_3,
  output out_4
);

  nand nand_1 (out_3, Set, out_4);
  nand nand_2 (out_4, out_3, Reset);
endmodule

module NAND_SR_Latch_w__Enable (
  input  Set,
  input  Enable,
  input  Reset,
  output Q,
  output Q_prime
);

  wire nand_1_out, nand_2_out;

  nand nand_1 (nand_1_out, Set, Enable);
  nand nand_2 (nand_2_out, Enable, Reset);
  NAND_SR_Latch nand_sr_latch_1 (.Set(nand_1_out), .Reset(nand_2_out), .out_3(Q), .out_4(Q_prime));
endmodule

module D_Latch (
  input  D,
  input  Enable,
  output Q,
  output Q_prime
);

  wire nand_1_out, nand_2_out, not_1_out;

  not not_1 (not_1_out, D);
  nand nand_1 (nand_1_out, D, Enable);
  nand nand_2 (nand_2_out, Enable, not_1_out);
  NAND_SR_Latch nand_sr_latch_1 (.Set(nand_1_out), .Reset(nand_2_out), .out_3(Q), .out_4(Q_prime));
endmodule

module Falling_Edge_Triggered_D_Flip_Flop (
  input  D,
  input  Clk,
  output Q,
  output Q_prime
);

  wire Master_q, not_1_out;

  D_Latch Master (.D(D), .Enable(Clk), .Q(Master_q));  // open: Q_prime
  not not_1 (not_1_out, Clk);
  D_Latch Slave (.D(Master_q), .Enable(not_1_out), .Q(Q), .Q_prime(Q_prime));
endmodule

module Positive_Edge_D_Flip_Flop (
  input  Clk,
  input  D,
  output Q,
  output Q_prime
);

  wire nand_1_out, nand_2_out, nand_3_out, nand_4_out;

  nand nand_1 (nand_1_out, nand_4_out, nand_2_out);
  nand nand_2 (nand_2_out, nand_1_out, Clk);
  nand nand_3 (nand_3_out, nand_2_out, Clk, nand_4_out);
  nand nand_4 (nand_4_out, nand_3_out, D);
  NAND_SR_Latch nand_sr_latch_1 (.Set(nand_2_out), .Reset(nand_3_out), .out_3(Q), .out_4(Q_prime));
endmodule

module JK_Flip_Flop (
  input  J,
  input  K,
  input  CLK,
  output Q,
  output Q_prime
);

  wire and_1_out, and_2_out, not_1_out, or_1_out;

  not not_1 (not_1_out, K);
  and and_1 (and_1_out, Q_prime, J);
  and and_2 (and_2_out, not_1_out, Q);
  or or_1 (or_1_out, and_1_out, and_2_out);
  Falling_Edge_Triggered_D_Flip_Flop falling_edge_triggered_d_flip_flop_1 (
    .D(or_1_out), .Clk(CLK), .Q(Q), .Q_prime(Q_prime));
endmodule

module T_Flip_Flop (
  input  T,
  input  Clk,
  output Q,
  output Q_prime
);

  JK_Flip_Flop jk_flip_flop_1 (.J(T), .K(T), .CLK(Clk), .Q(Q), .Q_prime(Q_prime));
endmodule
