// Logisim project registers_n_counters.circ as structural Verilog
module _4_bit_Serial_Adder (
  input  Shift_Control,
  input  Clock,
  input  Serial_In
);

  _4_bit_Shift_Register_w__Shift_Control u_4_bit_shift_register_w_shift_control_1 ();  // open: Serial_In, Shift_Control, Clock, Serial_Out
  _4_bit_Shift_Register_w__Shift_Control u_4_bit_shift_register_w_shift_control_2 ();  // open: Serial_In, Shift_Control, Clock, Serial_Out
  // AND_Gate and_1 is placed but not wired
  Full_Adder full_adder_1 ();  // open: A, B, carry_in, Sum, carry_out
  D_Flip_Flop d_ff_1 ();  // open: clk, D, Q, Qn, preset, en, reset
endmodule

module _4_bit_Shift_Register_w__Shift_Control (
  input  Serial_In,
  input  Shift_Control,
  input  Clock,
  output Serial_Out
);

  wire and_1_out, d_ff_1_q, d_ff_2_q, d_ff_3_q;

  and and_1 (and_1_out, Shift_Control, Clock);
  D_Flip_Flop d_ff_1 (.clk(and_1_out), .D(Serial_In), .Q(d_ff_1_q));  // open: Qn, preset, en, reset
  D_Flip_Flop d_ff_2 (.clk(and_1_out), .D(d_ff_1_q), .Q(d_ff_2_q));  // open: Qn, preset, en, reset
  D_Flip_Flop d_ff_3 (.clk(and_1_out), .D(d_ff_2_q), .Q(d_ff_3_q));  // open: Qn, preset, en, reset
  D_Flip_Flop d_ff_4 (.clk(and_1_out), .D(d_ff_3_q), .Qn(Serial_Out));  // open: Q, preset, en, reset
endmodule

module Full_Adder (
  input  A,
  input  B,
  input  carry_in,
  output Sum,
  output carry_out
);

  wire and_1_out, and_2_out, xor_1_out;

  and and_1 (and_1_out, B, A);
  xor xor_1 (xor_1_out, A, B);
  and and_2 (and_2_out, carry_in, xor_1_out);
  xor xor_2 (Sum, xor_1_out, carry_in);
  or or_1 (carry_out, and_2_out, and_1_out);
endmodule
