// Logisim project shift_by_2.circ as structural Verilog: 1 circuit, main circuit main
module main (
  input  in_1
);

  wire d_ff_1_q, d_ff_2_q, d_ff_3_q;

  D_Flip_Flop d_ff_1 (.clk(in_1), .D(1'b0), .Q(d_ff_1_q));  // open: Qn, preset, en, reset
  D_Flip_Flop d_ff_2 (.clk(in_1), .D(1'b0), .Q(d_ff_2_q));  // open: Qn, preset, en, reset
  D_Flip_Flop d_ff_3 (.clk(in_1), .D(d_ff_1_q), .Q(d_ff_3_q));  // open: Qn, preset, en, reset
  D_Flip_Flop d_ff_4 (.clk(in_1), .D(d_ff_2_q));  // open: Q, Qn, preset, en, reset
  D_Flip_Flop d_ff_5 (.clk(in_1), .D(d_ff_3_q));  // open: Q, Qn, preset, en, reset
endmodule
