// Logisim project Ex2.circ as structural Verilog: 1 circuit, main circuit main
module main (
  input  A,
  input  B,
  input  carry_in,
  output Sum,
  output carry_out
);

  wire and_1_out, and_2_out, xor_1_out;

  and and_1 (and_1_out, B, A);
  xor xor_1 (xor_1_out, A, B);
  and and_2 (and_2_out, carry_in, xor_1_out);
  xor xor_2 (Sum, xor_1_out, carry_in);
  or or_1 (carry_out, and_2_out, and_1_out);
endmodule
