// Logisim project Ex1.circ as structural Verilog: 3 circuits, main circuit main
module main (
  input  W,
  input  X,
  input  Y,
  input  Z,
  output \output 
);

  wire F1_output, F2_output;

  F1 F1 (.W(W), .X(X), .Y(Y), .Z(Z), .Output(F1_output));
  F2 F2 (.W(W), .X(X), .Y(Y), .Z(Z), .\output (F2_output));
  xnor xnor_1 (\output , F1_output, F2_output);
endmodule

module F1 (
  input  W,
  input  X,
  input  Y,
  input  Z,
  output Output
);

  wire not_1_out, not_2_out, not_3_out, not_4_out, not_5_out, w_prime_x_out, w_prime_xy_out, wx_out,
       wx_prime_out, wx_prime_y_out, wxy_out, x_prime_y_prime_out, x_prime_y_prime_z_out, xy_prime_out,
       xy_prime_z_out, xy_prime_z_z_prime_y_prime_z_out, xy_prime_z_z_prime_yz_w_prime_xy_out,
       zy_prime_z_z_prime_yz_w_prime_xy_wx_prime_y_out;

  not not_1 (not_1_out, Y);
  not not_2 (not_2_out, X);
  not not_3 (not_3_out, Y);
  and xy_prime (xy_prime_out, X, not_1_out);
  and x_prime_y_prime (x_prime_y_prime_out, not_2_out, not_3_out);
  not not_4 (not_4_out, W);
  and xy_prime_z (xy_prime_z_out, xy_prime_out, Z);
  and x_prime_y_prime_z (x_prime_y_prime_z_out, x_prime_y_prime_out, Z);
  and w_prime_x (w_prime_x_out, not_4_out, X);
  not not_5 (not_5_out, X);
  or xy_prime_z_z_prime_y_prime_z (xy_prime_z_z_prime_y_prime_z_out, xy_prime_z_out, x_prime_y_prime_z_out);
  and w_prime_xy (w_prime_xy_out, Y, w_prime_x_out);
  and wx_prime (wx_prime_out, W, not_5_out);
  or xy_prime_z_z_prime_yz_w_prime_xy (xy_prime_z_z_prime_yz_w_prime_xy_out, xy_prime_z_z_prime_y_prime_z_out, w_prime_xy_out);
  and wx_prime_y (wx_prime_y_out, Y, wx_prime_out);
  and wx (wx_out, W, X);
  or zy_prime_z_z_prime_yz_w_prime_xy_wx_prime_y (zy_prime_z_z_prime_yz_w_prime_xy_wx_prime_y_out, xy_prime_z_z_prime_yz_w_prime_xy_out, wx_prime_y_out);
  and wxy (wxy_out, Y, wx_out);
  or zy_prime_z_z_prime_yz_w_prime_xy_wx_prime_y_wxy (Output, zy_prime_z_z_prime_yz_w_prime_xy_wx_prime_y_out, wxy_out);
endmodule

module F2 (
  input  W,
  input  X,
  input  Y,
  input  Z,
  output \output 
);

  wire not_1_out, y_prime_z_out, y_prime_z_yx_out, yw_out, yx_out;

  not not_1 (not_1_out, Y);
  and y_prime_z (y_prime_z_out, not_1_out, Z);
  and yx (yx_out, Y, X);
  or y_prime_z_yx (y_prime_z_yx_out, y_prime_z_out, yx_out);
  and yw (yw_out, Y, W);
  or y_prime_z_yx_yw (\output , y_prime_z_yx_out, yw_out);
endmodule
