// Logisim project Ex2.circ as structural Verilog: 5 circuits, main circuit M_0
module main (
  input  [1:0] A,
  input  [1:0] B,
  output [3:0] out_3
);

  M_0 M_0 (.A_0(A[0]), .B_0(B[0]), .M_0(out_3[0]));
  M_1 M_1 (.A_0(A[0]), .A_1(A[1]), .B_0(B[0]), .B_1(B[1]), .M_1(out_3[1]));
  M_2 M_2 (.A_0(A[0]), .A_1(A[1]), .B_0(B[0]), .B_1(B[1]), .M_2(out_3[2]));
  M_3 M_3 (.A_0(A[0]), .A_1(A[1]), .B_0(B[0]), .B_1(B[1]), .M_3(out_3[3]));
endmodule

module M_0 (
  input  A_0,
  input  B_0,
  output M_0
);

  and A_0_B_0 (M_0, A_0, B_0);
endmodule

module M_1 (
  input  A_0,
  input  A_1,
  input  B_0,
  input  B_1,
  output M_1
);

  wire and_1_out, and_2_out;

  and and_1 (and_1_out, A_0, B_1);
  and and_2 (and_2_out, A_1, B_0);
  xor xor_1 (M_1, and_1_out, and_2_out);
endmodule

module M_2 (
  input  A_0,
  input  A_1,
  input  B_0,
  input  B_1,
  output M_2
);

  wire and_1_out, and_2_out;

  and and_1 (and_1_out, A_0, A_1, B_0, B_1);
  and and_2 (and_2_out, A_1, B_1);
  xor xor_1 (M_2, and_1_out, and_2_out);
endmodule

module M_3 (
  input  A_0,
  input  A_1,
  input  B_0,
  input  B_1,
  output M_3
);

  and and_1 (M_3, A_0, A_1, B_0, B_1);
endmodule
