// Logisim project Ex3.circ as structural Verilog: 4 circuits, main circuit main
module main (
  input  [2:0] A,
  input  [1:0] B,
  output [4:0] M
);

  wire A0B1_ab, A1B0_ab, A1B1_ab, A2B0_ab, A2B1_ab, M1_carry, M2_c_out;

  X_multiplier A0B0 (.A(A[0]), .B(B[0]), .AB(M[0]));
  X_multiplier A0B1 (.A(A[0]), .B(B[1]), .AB(A0B1_ab));
  X_multiplier A1B0 (.A(A[1]), .B(B[0]), .AB(A1B0_ab));
  X_multiplier A1B1 (.A(A[1]), .B(B[1]), .AB(A1B1_ab));
  X_multiplier A2B0 (.A(A[2]), .B(B[0]), .AB(A2B0_ab));
  X_multiplier A2B1 (.A(A[2]), .B(B[1]), .AB(A2B1_ab));
  half_adder M1 (.A(A0B1_ab), .B(A1B0_ab), .Sum(M[1]), .Carry(M1_carry));
  full_adder M2 (.a(A1B1_ab), .b(A2B0_ab), .c(M1_carry), .Sum(M[2]), .c_out(M2_c_out));
  half_adder M3 (.A(A2B1_ab), .B(M2_c_out), .Sum(M[3]), .Carry(M[4]));
endmodule

module X_multiplier (
  input  A,
  input  B,
  output AB
);

  and and_1 (AB, A, B);
endmodule

module full_adder (
  input  a,
  input  b,
  input  c,
  output Sum,
  output c_out
);

  wire AND_2_out, AND_out, XOR_out;

  and AND (AND_out, b, a);
  xor XOR (XOR_out, a, b);
  and AND_2 (AND_2_out, c, XOR_out);
  xor XOR_2 (Sum, XOR_out, c);
  or OR (c_out, AND_2_out, AND_out);
endmodule

module half_adder (
  input  A,
  input  B,
  output Sum,
  output Carry
);

  and and_1 (Carry, B, A);
  xor xor_1 (Sum, A, B);
endmodule
