// Logisim project Lab3_Ex1.circ as structural Verilog
module main (
  input  [3:0] A,
  output P,
  output D
);

  Function_P Function_P (.A3(A[3]), .A2(A[2]), .A1(A[1]), .A0(A[0]), .P(P));
  Function_D Function_D (.A3(A[3]), .A2(A[2]), .A1(A[1]), .A0(A[0]), .D(D));
endmodule

module Function_P (
  input  A3,
  input  A2,
  input  A1,
  input  A0,
  output P
);

  wire and_1_out, and_2_out, and_3_out, and_4_out, not_1_out, not_2_out, not_3_out, not_4_out, not_5_out;

  not not_1 (not_1_out, A2);
  not not_2 (not_2_out, A3);
  not not_3 (not_3_out, A2);
  not not_4 (not_4_out, A3);
  not not_5 (not_5_out, A1);
  and and_1 (and_1_out, not_1_out, A1, A0);
  and and_2 (and_2_out, not_2_out, not_3_out, A1);
  and and_3 (and_3_out, not_4_out, A2, A0);
  and and_4 (and_4_out, A2, not_5_out, A0);
  or or_1 (P, and_1_out, and_2_out, and_3_out, and_4_out);
endmodule

module Function_D (
  input  A3,
  input  A2,
  input  A1,
  input  A0,
  output D
);

  wire and_1_out, and_2_out, and_3_out, and_4_out, and_5_out, not_1_out, not_2_out, not_3_out, not_4_out,
       not_5_out, not_6_out, not_7_out;

  not not_1 (not_1_out, A3);
  not not_2 (not_2_out, A2);
  not not_3 (not_3_out, A1);
  not not_4 (not_4_out, A1);
  not not_5 (not_5_out, A0);
  not not_6 (not_6_out, A3);
  not not_7 (not_7_out, A2);
  and and_1 (and_1_out, not_1_out, A2, A0);
  and and_2 (and_2_out, A3, not_2_out, not_3_out);
  and and_3 (and_3_out, A3, not_4_out, not_5_out);
  and and_4 (and_4_out, not_6_out, not_7_out, A1, A0);
  and and_5 (and_5_out, A3, A2, A1, A0);
  or or_1 (D, and_1_out, and_2_out, and_3_out, and_4_out, and_5_out);
endmodule

module Combinational_Circuit (
  input  A3,
  input  A2,
  input  A1,
  input  A0,
  output P,
  output D
);

  wire and_1_out, and_2_out, and_3_out, and_4_out, and_5_out, and_6_out, and_7_out, and_8_out, and_9_out,
       not_1_out, not_2_out, not_3_out, not_4_out, not_5_out, not_6_out, not_7_out, not_8_out, not_9_out,
       not_10_out, not_11_out, not_12_out, not_13_out;

  not not_1 (not_1_out, A3);
  and and_1 (and_1_out, not_1_out, not_2_out, A1);
  not not_2 (not_2_out, A2);
  not not_3 (not_3_out, A2);
  and and_2 (and_2_out, not_3_out, A1, A0);
  not not_4 (not_4_out, A3);
  and and_3 (and_3_out, not_4_out, A2, A0);
  and and_4 (and_4_out, A2, not_5_out, A0);
  not not_5 (not_5_out, A1);
  not not_6 (not_6_out, A3);
  not not_7 (not_7_out, A2);
  not not_8 (not_8_out, A3);
  not not_9 (not_9_out, A0);
  not not_10 (not_10_out, A2);
  not not_11 (not_11_out, A1);
  not not_12 (not_12_out, A1);
  not not_13 (not_13_out, A0);
  or or_1 (P, and_1_out, and_2_out, and_3_out, and_4_out);
  and and_5 (and_5_out, not_6_out, not_7_out, A1, A0);
  and and_6 (and_6_out, not_8_out, A2, not_9_out);
  and and_7 (and_7_out, A3, not_10_out, not_11_out);
  and and_8 (and_8_out, A3, not_12_out, not_13_out);
  and and_9 (and_9_out, A3, A2, A1, A0);
  or or_2 (D, and_5_out, and_6_out, and_7_out, and_8_out, and_9_out);
  LED led_1 (.in(P));
  LED led_2 (.in(D));
endmodule
