// Logisim project Lab4_Ex1.circ as structural Verilog
module main (
  input  Carry_in,
  input  [3:0] A,
  input  [3:0] B,
  input  S2,
  input  S1,
  input  S0,
  output C_out,
  output S,
  output V
);

  wire n7_segment_decoder_1_sa, n7_segment_decoder_1_sb, n7_segment_decoder_1_sc, n7_segment_decoder_1_sd,
       n7_segment_decoder_1_se, n7_segment_decoder_1_sf, n7_segment_decoder_1_sg,
       n8_mux_function_switcher_1_f0, n8_mux_function_switcher_1_f1, n8_mux_function_switcher_1_f2,
       n8_mux_function_switcher_1_f3;

  _8_MUX_Function_Switcher u_8_mux_function_switcher_1 (
    .Carry__in(Carry_in), .S2(S2), .A3(A[3]), .S1(S1), .A2(A[2]), .S0(S0), .A1(A[1]), .A0(A[0]), .B3(B[3]),
    .B2(B[2]), .B1(B[1]), .B0(B[0]), .F3(n8_mux_function_switcher_1_f3), .F2(n8_mux_function_switcher_1_f2),
    .F1(n8_mux_function_switcher_1_f1), .F0(n8_mux_function_switcher_1_f0), .FC(C_out), .FS(S), .FV(V));
  _7_Segment_Decoder u_7_segment_decoder_1 (
    .D3(n8_mux_function_switcher_1_f3), .D2(n8_mux_function_switcher_1_f2),
    .D1(n8_mux_function_switcher_1_f1), .D0(n8_mux_function_switcher_1_f0), .Sa(n7_segment_decoder_1_sa),
    .Sb(n7_segment_decoder_1_sb), .Sc(n7_segment_decoder_1_sc), .Sd(n7_segment_decoder_1_sd),
    .Se(n7_segment_decoder_1_se), .Sf(n7_segment_decoder_1_sf), .Sg(n7_segment_decoder_1_sg));
  _7_Segment_Display u_7_segment_display_1 (
    .g(n7_segment_decoder_1_sg), .f(n7_segment_decoder_1_sf), .a(n7_segment_decoder_1_sa),
    .b(n7_segment_decoder_1_sb), .e(n7_segment_decoder_1_se), .d(n7_segment_decoder_1_sd),
    .c(n7_segment_decoder_1_sc));  // open: dp
endmodule

module _8bit_to_1bit_MUX_prototype (
  input  AND,
  input  OR,
  input  XOR,
  input  XNOR,
  input  A_1,
  input  A_B,
  input  A_B_2,
  input  B_A,
  input  S2,
  input  S1,
  input  S0,
  output F
);

  wire and_1_out, and_2_out, and_3_out, and_4_out, and_5_out, and_6_out, and_7_out, and_8_out, not_1_out,
       not_2_out, not_3_out, not_4_out, not_5_out, not_6_out, not_7_out, not_8_out, not_9_out, not_10_out,
       not_11_out, not_12_out;

  not not_1 (not_1_out, S2);
  not not_2 (not_2_out, S1);
  not not_3 (not_3_out, S0);
  not not_4 (not_4_out, S2);
  not not_5 (not_5_out, S1);
  not not_6 (not_6_out, S2);
  not not_7 (not_7_out, S0);
  not not_8 (not_8_out, S2);
  not not_9 (not_9_out, S1);
  not not_10 (not_10_out, S0);
  not not_11 (not_11_out, S1);
  not not_12 (not_12_out, S0);
  and and_1 (and_1_out, AND, not_1_out, not_2_out, not_3_out);
  and and_2 (and_2_out, OR, not_4_out, not_5_out, S0);
  and and_3 (and_3_out, XOR, not_6_out, S1, not_7_out);
  and and_4 (and_4_out, XNOR, not_8_out, S1, S0);
  and and_5 (and_5_out, A_1, S2, not_9_out, not_10_out);
  and and_6 (and_6_out, A_B, S2, not_11_out, S0);
  and and_7 (and_7_out, A_B_2, S2, S1, not_12_out);
  and and_8 (and_8_out, B_A, S2, S1, S0);
  or or_1 (F, and_1_out, and_2_out, and_3_out, and_4_out, and_5_out, and_6_out, and_7_out, and_8_out);
endmodule

module AND (
  input  A3,
  input  A2,
  input  A1,
  input  A0,
  input  B3,
  input  B2,
  input  B1,
  input  B0,
  output O3,
  output O2,
  output O1,
  output O0
);

  and _3 (O3, A3, B3);
  and _2 (O2, A2, B2);
  and _1 (O1, A1, B1);
  and _0 (O0, A0, B0);
endmodule

module OR (
  input  A3,
  input  A2,
  input  A1,
  input  A0,
  input  B3,
  input  B2,
  input  B1,
  input  B0,
  output O3,
  output O2,
  output O1,
  output O0
);

  or or_1 (O3, A3, B3);
  or or_2 (O2, A2, B2);
  or or_3 (O1, A1, B1);
  or or_4 (O0, A0, B0);
endmodule

module XOR (
  input  A3,
  input  A2,
  input  A1,
  input  A0,
  input  B3,
  input  B2,
  input  B1,
  input  B0,
  output O3,
  output O2,
  output O1,
  output O0
);

  xor xor_1 (O3, A3, B3);
  xor xor_2 (O2, A2, B2);
  xor xor_3 (O1, A1, B1);
  xor xor_4 (O0, A0, B0);
endmodule

module XNOR (
  input  A3,
  input  A2,
  input  A1,
  input  A0,
  input  B3,
  input  B2,
  input  B1,
  input  B0,
  output O3,
  output O2,
  output O1,
  output O0
);

  xnor xnor_1 (O3, A3, B3);
  xnor xnor_2 (O2, A2, B2);
  xnor xnor_3 (O1, A1, B1);
  xnor xnor_4 (O0, A0, B0);
endmodule

module A_1 (
  input  Carry_in,
  input  A3,
  input  A2,
  input  A1,
  input  A0,
  output O3,
  output O2,
  output O1,
  output O0,
  output Carry_out,
  output Overflow
);

  _4_bit_adder u_4_bit_adder_1 (
    .Carry_in(Carry_in), .A0(A0), .A1(A1), .A2(A2), .A3(A3), .B0(1'b1), .B1(1'b0), .B2(1'b0), .B3(1'b0),
    .O0(O0), .O1(O1), .O2(O2), .O3(O3), .Carry_out(Carry_out), .Overflow(Overflow));
endmodule

module A_B_2 (
  input  Carry_in,
  input  A0,
  input  A1,
  input  A2,
  input  A3,
  input  B0,
  input  B1,
  input  B2,
  input  B3,
  output O3,
  output O2,
  output O1,
  output O0,
  output Carry_out,
  output Sign_bit,
  output Overflow
);

  wire n4_bit_adder_1_o0, n4_bit_adder_1_o1, n4_bit_adder_1_o2, two_s_complement_1_o0, two_s_complement_1_o1,
       two_s_complement_1_o2, two_s_complement_1_o3;

  Two_s_Complement two_s_complement_1 (
    .Carry_in(1'b0), .A3(B3), .A2(B2), .A1(B1), .A0(B0), .O3(two_s_complement_1_o3),
    .O2(two_s_complement_1_o2), .O1(two_s_complement_1_o1), .O0(two_s_complement_1_o0));
  _4_bit_adder u_4_bit_adder_1 (
    .Carry_in(Carry_in), .A0(A0), .A1(A1), .A2(A2), .A3(A3), .B0(two_s_complement_1_o0),
    .B1(two_s_complement_1_o1), .B2(two_s_complement_1_o2), .B3(two_s_complement_1_o3),
    .O0(n4_bit_adder_1_o0), .O1(n4_bit_adder_1_o1), .O2(n4_bit_adder_1_o2), .O3(Sign_bit),
    .Carry_out(Carry_out), .Overflow(Overflow));
  Negative_Number_Corrector negative_number_corrector_1 (
    .A3(Sign_bit), .A2(n4_bit_adder_1_o2), .A1(n4_bit_adder_1_o1), .A0(n4_bit_adder_1_o0), .S(Sign_bit),
    .O3(O3), .O2(O2), .O1(O1), .O0(O0));
endmodule

module _4_bit_adder (
  input  Carry_in,
  input  A0,
  input  A1,
  input  A2,
  input  A3,
  input  B0,
  input  B1,
  input  B2,
  input  B3,
  output O0,
  output O1,
  output O2,
  output O3,
  output Carry_out,
  output Overflow
);

  wire n1_bit_full_adder_1_c_out, n1_bit_full_adder_2_c_out, n1_bit_full_adder_3_c_out;

  _1_bit_full_adder u_1_bit_full_adder_1 (.a(A0), .b(B0), .c(Carry_in), .Sum(O0), .c_out(n1_bit_full_adder_1_c_out));
  _1_bit_full_adder u_1_bit_full_adder_2 (
    .a(A1), .b(B1), .c(n1_bit_full_adder_1_c_out), .Sum(O1), .c_out(n1_bit_full_adder_2_c_out));
  _1_bit_full_adder u_1_bit_full_adder_3 (
    .a(A2), .b(B2), .c(n1_bit_full_adder_2_c_out), .Sum(O2), .c_out(n1_bit_full_adder_3_c_out));
  _1_bit_full_adder u_1_bit_full_adder_4 (.a(A3), .b(B3), .c(n1_bit_full_adder_3_c_out), .Sum(O3), .c_out(Carry_out));
  xor xor_1 (Overflow, n1_bit_full_adder_3_c_out, Carry_out);
endmodule

module _1_bit_full_adder (
  input  a,
  input  b,
  input  c,
  output Sum,
  output c_out
);

  wire AND_2_out, AND_out, XOR_out;

  and AND (AND_out, b, a);
  xor XOR (XOR_out, a, b);
  and AND_2 (AND_2_out, c, XOR_out);
  xor XOR_2 (Sum, XOR_out, c);
  or OR (c_out, AND_2_out, AND_out);
endmodule

module _7_Segment_Decoder (
  input  D3,
  input  D2,
  input  D1,
  input  D0,
  output Sa,
  output Sb,
  output Sc,
  output Sd,
  output Se,
  output Sf,
  output Sg
);

  wire and_1_out, and_2_out, and_3_out, and_4_out, and_5_out, and_6_out, and_7_out, and_8_out, and_9_out,
       and_10_out, and_11_out, and_12_out, and_13_out, and_14_out, not_1_out, not_2_out, not_3_out,
       not_4_out, not_5_out, not_6_out, not_7_out, not_8_out, not_9_out, not_10_out, not_11_out, not_12_out,
       not_13_out, not_14_out, not_15_out, not_16_out, not_17_out, not_18_out, not_19_out, not_20_out,
       or_2_out;

  not not_1 (not_1_out, D2);
  and and_1 (and_1_out, not_1_out, not_2_out);
  not not_2 (not_2_out, D0);
  and and_2 (and_2_out, D2, D0);
  not not_3 (not_3_out, D2);
  not not_4 (not_4_out, D1);
  and and_3 (and_3_out, not_4_out, not_5_out);
  not not_5 (not_5_out, D0);
  and and_4 (and_4_out, D1, D0);
  not not_6 (not_6_out, D1);
  or or_1 (Sc, not_6_out, D0, D2);
  not not_7 (not_7_out, D2);
  and and_5 (and_5_out, not_7_out, not_8_out);
  not not_8 (not_8_out, D0);
  not not_9 (not_9_out, D2);
  and and_6 (and_6_out, not_9_out, D1);
  and and_7 (and_7_out, D1, not_10_out);
  not not_10 (not_10_out, D0);
  not not_11 (not_11_out, D1);
  and and_8 (and_8_out, D2, not_11_out, D0);
  not not_12 (not_12_out, D0);
  not not_13 (not_13_out, D2);
  or or_2 (or_2_out, not_13_out, D1);
  not not_14 (not_14_out, D1);
  and and_9 (and_9_out, not_14_out, not_15_out);
  not not_15 (not_15_out, D0);
  and and_10 (and_10_out, D2, not_16_out);
  not not_16 (not_16_out, D1);
  and and_11 (and_11_out, D2, not_17_out);
  not not_17 (not_17_out, D0);
  not not_18 (not_18_out, D2);
  and and_12 (and_12_out, not_18_out, D1);
  and and_13 (and_13_out, D1, not_19_out);
  not not_19 (not_19_out, D0);
  and and_14 (and_14_out, D2, not_20_out);
  not not_20 (not_20_out, D1);
  or or_3 (Sa, and_1_out, D1, and_2_out, D3);
  or or_4 (Sb, not_3_out, and_3_out, and_4_out);
  or or_5 (Sd, and_5_out, and_6_out, and_7_out, and_8_out, D3);
  and and_15 (Se, not_12_out, or_2_out);
  or or_6 (Sf, and_9_out, and_10_out, and_11_out, D3);
  or or_7 (Sg, and_12_out, and_13_out, and_14_out, D3);
  _7_Segment_Display u_7_segment_display_1 (.g(Sg), .f(Sf), .a(Sa), .b(Sb), .e(Se), .d(Sd), .c(Sc));  // open: dp
endmodule

module _8_MUX_Function_Switcher (
  input  Carry__in,
  input  S2,
  input  A3,
  input  S1,
  input  A2,
  input  S0,
  input  A1,
  input  A0,
  input  B3,
  input  B2,
  input  B1,
  input  B0,
  output F3,
  output F2,
  output F1,
  output F0,
  output FC,
  output FS,
  output FV
);

  wire A_1_carry_out, A_1_o0, A_1_o1, A_1_o2, A_1_o3, A_1_overflow, A_B_2_carry_out, A_B_2_o0, A_B_2_o1,
       A_B_2_o2, A_B_2_o3, A_B_2_overflow, A_B_2_sign_bit, A_B_carry_out, A_B_o0, A_B_o1, A_B_o2, A_B_o3,
       A_B_overflow, AND_o0, AND_o1, AND_o2, AND_o3, B_A_carry_out, B_A_o0, B_A_o1, B_A_o2, B_A_o3,
       B_A_overflow, B_A_sign_bit, OR_o0, OR_o1, OR_o2, OR_o3, XNOR_o0, XNOR_o1, XNOR_o2, XNOR_o3, XOR_o0,
       XOR_o1, XOR_o2, XOR_o3;

  AND AND (
    .A3(A3), .A2(A2), .A1(A1), .A0(A0), .B3(B3), .B2(B2), .B1(B1), .B0(B0), .O3(AND_o3), .O2(AND_o2),
    .O1(AND_o1), .O0(AND_o0));
  OR OR (
    .A3(A3), .A2(A2), .A1(A1), .A0(A0), .B3(B3), .B2(B2), .B1(B1), .B0(B0), .O3(OR_o3), .O2(OR_o2),
    .O1(OR_o1), .O0(OR_o0));
  XOR XOR (
    .A3(A3), .A2(A2), .A1(A1), .A0(A0), .B3(B3), .B2(B2), .B1(B1), .B0(B0), .O3(XOR_o3), .O2(XOR_o2),
    .O1(XOR_o1), .O0(XOR_o0));
  XNOR XNOR (
    .A3(A3), .A2(A2), .A1(A1), .A0(A0), .B3(B3), .B2(B2), .B1(B1), .B0(B0), .O3(XNOR_o3), .O2(XNOR_o2),
    .O1(XNOR_o1), .O0(XNOR_o0));
  A_1 A_1 (
    .Carry_in(Carry__in), .A3(A3), .A2(A2), .A1(A1), .A0(A0), .O3(A_1_o3), .O2(A_1_o2), .O1(A_1_o1),
    .O0(A_1_o0), .Carry_out(A_1_carry_out), .Overflow(A_1_overflow));
  _4_bit_adder A_B (
    .Carry_in(Carry__in), .A0(A0), .A1(A1), .A2(A2), .A3(A3), .B0(B0), .B1(B1), .B2(B2), .B3(B3),
    .O0(A_B_o0), .O1(A_B_o1), .O2(A_B_o2), .O3(A_B_o3), .Carry_out(A_B_carry_out), .Overflow(A_B_overflow));
  A_B_2 A_B_2 (
    .Carry_in(Carry__in), .A0(A0), .A1(A1), .A2(A2), .A3(A3), .B0(B0), .B1(B1), .B2(B2), .B3(B3),
    .O3(A_B_2_o3), .O2(A_B_2_o2), .O1(A_B_2_o1), .O0(A_B_2_o0), .Carry_out(A_B_2_carry_out),
    .Sign_bit(A_B_2_sign_bit), .Overflow(A_B_2_overflow));
  A_B_2 B_A (
    .Carry_in(Carry__in), .A0(B0), .A1(B1), .A2(B2), .A3(B3), .B0(A0), .B1(A1), .B2(A2), .B3(A3),
    .O3(B_A_o3), .O2(B_A_o2), .O1(B_A_o1), .O0(B_A_o0), .Carry_out(B_A_carry_out), .Sign_bit(B_A_sign_bit),
    .Overflow(B_A_overflow));
  _8bit_to_1bit_MUX_prototype MUX3 (
    .AND(AND_o3), .OR(OR_o3), .XOR(XOR_o3), .XNOR(XNOR_o3), .A_1(A_1_o3), .A_B(A_B_o3), .A_B_2(A_B_2_o3),
    .B_A(B_A_o3), .S2(S2), .S1(S1), .S0(S0), .F(F3));
  _8bit_to_1bit_MUX_prototype MUX2 (
    .AND(AND_o2), .OR(OR_o2), .XOR(XOR_o2), .XNOR(XNOR_o2), .A_1(A_1_o2), .A_B(A_B_o2), .A_B_2(A_B_2_o2),
    .B_A(B_A_o2), .S2(S2), .S1(S1), .S0(S0), .F(F2));
  _8bit_to_1bit_MUX_prototype MUX1 (
    .AND(AND_o1), .OR(OR_o1), .XOR(XOR_o1), .XNOR(XNOR_o1), .A_1(A_1_o1), .A_B(A_B_o1), .A_B_2(A_B_2_o1),
    .B_A(B_A_o1), .S2(S2), .S1(S1), .S0(S0), .F(F1));
  _8bit_to_1bit_MUX_prototype MUX0 (
    .AND(AND_o0), .OR(OR_o0), .XOR(XOR_o0), .XNOR(XNOR_o0), .A_1(A_1_o0), .A_B(A_B_o0), .A_B_2(A_B_2_o0),
    .B_A(B_A_o0), .S2(S2), .S1(S1), .S0(S0), .F(F0));
  _8bit_to_1bit_MUX_prototype MUXC (
    .AND(1'b0), .OR(1'b0), .XOR(1'b0), .XNOR(1'b0), .A_1(A_1_carry_out), .A_B(A_B_carry_out),
    .A_B_2(A_B_2_carry_out), .B_A(B_A_carry_out), .S2(S2), .S1(S1), .S0(S0), .F(FC));
  _8bit_to_1bit_MUX_prototype MUXS (
    .AND(1'b0), .OR(1'b0), .XOR(1'b0), .XNOR(1'b0), .A_1(1'b0), .A_B(1'b0), .A_B_2(A_B_2_sign_bit),
    .B_A(B_A_sign_bit), .S2(S2), .S1(S1), .S0(S0), .F(FS));
  _8bit_to_1bit_MUX_prototype MUXV (
    .AND(1'b0), .OR(1'b0), .XOR(1'b0), .XNOR(1'b0), .A_1(A_1_overflow), .A_B(A_B_overflow),
    .A_B_2(A_B_2_overflow), .B_A(B_A_overflow), .S2(S2), .S1(S1), .S0(S0), .F(FV));
endmodule

module Two_s_Complement (
  input  Carry_in,
  input  A3,
  input  A2,
  input  A1,
  input  A0,
  output O3,
  output O2,
  output O1,
  output O0
);

  wire not_1_out, not_2_out, not_3_out, not_4_out;

  not not_1 (not_1_out, A3);
  not not_2 (not_2_out, A2);
  not not_3 (not_3_out, A1);
  not not_4 (not_4_out, A0);
  A_1 A_1 (
    .Carry_in(Carry_in), .A3(not_1_out), .A2(not_2_out), .A1(not_3_out), .A0(not_4_out), .O3(O3), .O2(O2),
    .O1(O1), .O0(O0));  // open: Carry_out, Overflow
endmodule

module Negative_Number_Corrector (
  input  A3,
  input  A2,
  input  A1,
  input  A0,
  input  S,
  output O3,
  output O2,
  output O1,
  output O0
);

  wire two_s_complement_1_o0, two_s_complement_1_o1, two_s_complement_1_o2, two_s_complement_1_o3;

  Two_s_Complement two_s_complement_1 (
    .Carry_in(1'b0), .A3(A3), .A2(A2), .A1(A1), .A0(A0), .O3(two_s_complement_1_o3),
    .O2(two_s_complement_1_o2), .O1(two_s_complement_1_o1), .O0(two_s_complement_1_o0));
  _2bit_to_1bit_MUX _3 (.S(S), .Unmodified(A3), .Two_s_Comp(two_s_complement_1_o3), .O(O3));
  _2bit_to_1bit_MUX _2 (.S(S), .Unmodified(A2), .Two_s_Comp(two_s_complement_1_o2), .O(O2));
  _2bit_to_1bit_MUX _1 (.S(S), .Unmodified(A1), .Two_s_Comp(two_s_complement_1_o1), .O(O1));
  _2bit_to_1bit_MUX _0 (.S(S), .Unmodified(A0), .Two_s_Comp(two_s_complement_1_o0), .O(O0));
endmodule

module _2bit_to_1bit_MUX (
  input  S,
  input  Unmodified,
  input  Two_s_Comp,
  output O
);

  wire and_1_out, and_2_out, not_1_out;

  not not_1 (not_1_out, S);
  and and_1 (and_1_out, not_1_out, Unmodified);
  and and_2 (and_2_out, S, Two_s_Comp);
  or or_1 (O, and_1_out, and_2_out);
endmodule
