// Logisim project Lab5_Ex1.circ as structural Verilog
module main (
);

  wire _7_Segment_Decoder_sa, _7_Segment_Decoder_sb, _7_Segment_Decoder_sc, _7_Segment_Decoder_sd,
       _7_Segment_Decoder_se, _7_Segment_Decoder_sf, _7_Segment_Decoder_sg, Binary_Counter_a,
       Binary_Counter_b, Binary_Counter_c, clock_1_out;

  Clock clock_1 (.out(clock_1_out));
  Binary_Counter Binary_Counter (.Clock(clock_1_out), .A(Binary_Counter_a), .B(Binary_Counter_b), .C(Binary_Counter_c));
  BCD_to_7_Segment_Decoder _7_Segment_Decoder (
    .D3(1'b0), .D2(Binary_Counter_a), .D1(Binary_Counter_b), .D0(Binary_Counter_c),
    .Sa(_7_Segment_Decoder_sa), .Sb(_7_Segment_Decoder_sb), .Sc(_7_Segment_Decoder_sc),
    .Sd(_7_Segment_Decoder_sd), .Se(_7_Segment_Decoder_se), .Sf(_7_Segment_Decoder_sf),
    .Sg(_7_Segment_Decoder_sg));
  _7_Segment_Display u_7_segment_display_1 (
    .g(_7_Segment_Decoder_sg), .f(_7_Segment_Decoder_sf), .a(_7_Segment_Decoder_sa),
    .b(_7_Segment_Decoder_sb), .e(_7_Segment_Decoder_se), .d(_7_Segment_Decoder_sd), .c(_7_Segment_Decoder_sc));  // open: dp
endmodule

module Binary_Counter (
  input  Clock,
  output A,
  output B,
  output C
);

  wire Combinational_da, Combinational_db, Combinational_dc;

  Combinational_Circuit Combinational (
    .A(A), .B(B), .C(C), .Da(Combinational_da), .Db(Combinational_db), .Dc(Combinational_dc));
  D_Flip_Flop d_ff_1 (.clk(Clock), .D(Combinational_da), .Q(A));  // open: Qn, preset, en, reset
  D_Flip_Flop d_ff_2 (.clk(Clock), .D(Combinational_db), .Q(B));  // open: Qn, preset, en, reset
  D_Flip_Flop d_ff_3 (.clk(Clock), .D(Combinational_dc), .Q(C));  // open: Qn, preset, en, reset
endmodule

module Combinational_Circuit (
  input  A,
  input  B,
  input  C,
  output Da,
  output Db,
  output Dc
);

  Da u_Da (.A(A), .B(B), .C(C), .Da(Da));
  Db u_Db (.A(A), .B(B), .C(C), .Db(Db));
  Dc u_Dc (.A(A), .B(B), .C(C), .Dc(Dc));
endmodule

module Da (
  input  A,
  input  B,
  input  C,
  output Da
);

  wire and_1_out, and_2_out, not_1_out;

  not not_1 (not_1_out, B);
  and and_1 (and_1_out, A, not_1_out);
  and and_2 (and_2_out, B, C);
  or or_1 (Da, and_1_out, and_2_out);
endmodule

module Db (
  input  A,
  input  B,
  input  C,
  output Db
);

  wire and_1_out, and_2_out, not_1_out, not_2_out, not_3_out;

  not not_1 (not_1_out, B);
  and and_1 (and_1_out, not_1_out, C);
  not not_2 (not_2_out, A);
  and and_2 (and_2_out, not_2_out, B, not_3_out);
  not not_3 (not_3_out, C);
  or or_1 (Db, and_1_out, and_2_out);
endmodule

module Dc (
  input  A,
  input  B,
  input  C,
  output Dc
);

  wire nor_1_out, nor_2_out;

  nor nor_1 (nor_1_out, B, C);
  nor nor_2 (nor_2_out, A, C);
  or or_1 (Dc, nor_1_out, nor_2_out);
endmodule

module BCD_to_7_Segment_Decoder (
  input  D3,
  input  D2,
  input  D1,
  input  D0,
  output Sa,
  output Sb,
  output Sc,
  output Sd,
  output Se,
  output Sf,
  output Sg
);

  wire and_1_out, and_2_out, and_3_out, and_4_out, and_5_out, and_6_out, and_7_out, and_8_out, and_9_out,
       and_10_out, and_11_out, and_12_out, and_13_out, and_14_out, not_1_out, not_2_out, not_3_out,
       not_4_out, not_5_out, not_6_out, not_7_out, not_8_out, not_9_out, not_10_out, not_11_out, not_12_out,
       not_13_out, not_14_out, not_15_out, not_16_out, not_17_out, not_18_out, not_19_out, not_20_out,
       or_2_out;

  not not_1 (not_1_out, D2);
  and and_1 (and_1_out, not_1_out, not_2_out);
  not not_2 (not_2_out, D0);
  and and_2 (and_2_out, D2, D0);
  not not_3 (not_3_out, D2);
  not not_4 (not_4_out, D1);
  and and_3 (and_3_out, not_4_out, not_5_out);
  not not_5 (not_5_out, D0);
  and and_4 (and_4_out, D1, D0);
  not not_6 (not_6_out, D1);
  or or_1 (Sc, not_6_out, D0, D2);
  not not_7 (not_7_out, D2);
  and and_5 (and_5_out, not_7_out, not_8_out);
  not not_8 (not_8_out, D0);
  not not_9 (not_9_out, D2);
  and and_6 (and_6_out, not_9_out, D1);
  and and_7 (and_7_out, D1, not_10_out);
  not not_10 (not_10_out, D0);
  and and_8 (and_8_out, D2, not_11_out, D0);
  not not_11 (not_11_out, D1);
  not not_12 (not_12_out, D0);
  not not_13 (not_13_out, D2);
  or or_2 (or_2_out, not_13_out, D1);
  not not_14 (not_14_out, D1);
  and and_9 (and_9_out, not_14_out, not_15_out);
  not not_15 (not_15_out, D0);
  and and_10 (and_10_out, D2, not_16_out);
  not not_16 (not_16_out, D1);
  and and_11 (and_11_out, D2, not_17_out);
  not not_17 (not_17_out, D0);
  not not_18 (not_18_out, D2);
  and and_12 (and_12_out, not_18_out, D1);
  and and_13 (and_13_out, D1, not_19_out);
  not not_19 (not_19_out, D0);
  and and_14 (and_14_out, D2, not_20_out);
  not not_20 (not_20_out, D1);
  or or_3 (Sa, and_1_out, D1, and_2_out, D3);
  or or_4 (Sb, not_3_out, and_3_out, and_4_out);
  or or_5 (Sd, and_5_out, and_6_out, and_7_out, and_8_out, D3);
  and and_15 (Se, not_12_out, or_2_out);
  or or_6 (Sf, and_9_out, and_10_out, and_11_out, D3);
  or or_7 (Sg, and_12_out, and_13_out, and_14_out, D3);
  _7_Segment_Display u_7_segment_display_1 (.g(Sg), .f(Sf), .a(Sa), .b(Sb), .e(Se), .d(Sd), .c(Sc));  // open: dp
endmodule
