// Logisim project Lab5_Ex2.circ as structural Verilog
module Sequence_Detector (
  input  x,
  input  Clock,
  output y
);

  wire Next_State_Comb_da, Next_State_Comb_db, Next_State_Comb_dc, State_Register_a, State_Register_b,
       State_Register_c;

  Next_State_Combinational Next_State_Comb (
    .A(State_Register_a), .B(State_Register_b), .C(State_Register_c), .x(x), .Da(Next_State_Comb_da),
    .Db(Next_State_Comb_db), .Dc(Next_State_Comb_dc));
  Clock clock_1 (.out(Clock));
  State_Register State_Register (
    .Da(Next_State_Comb_da), .Db(Next_State_Comb_db), .Dc(Next_State_Comb_dc), .Clock(Clock),
    .A(State_Register_a), .B(State_Register_b), .C(State_Register_c));
  Output_Combinational Output_Comb (.A(State_Register_a), .B(State_Register_b), .C(State_Register_c), .y(y));
endmodule

module Next_State_Combinational (
  input  A,
  input  B,
  input  C,
  input  x,
  output Da,
  output Db,
  output Dc
);

  Da u_Da (.B(B), .C(C), .x(x), .Da(Da));
  Db u_Db (.A(A), .B(B), .C(C), .x(x), .Db(Db));
  Dc u_Dc (.A(A), .B(B), .C(C), .x(x), .Dc(Dc));
endmodule

module Da (
  input  B,
  input  C,
  input  x,
  output Da
);

  and and_1 (Da, B, C, x);
endmodule

module Db (
  input  A,
  input  B,
  input  C,
  input  x,
  output Db
);

  wire nand_1_out, or_1_out, or_2_out;

  or or_1 (or_1_out, A, B, C);
  nand nand_1 (nand_1_out, B, C);
  or or_2 (or_2_out, B, x);
  and and_1 (Db, or_1_out, nand_1_out, or_2_out);
endmodule

module Dc (
  input  A,
  input  B,
  input  C,
  input  x,
  output Dc
);

  wire nand_1_out, not_1_out, not_2_out, or_1_out;

  or or_1 (or_1_out, B, x);
  nand nand_1 (nand_1_out, B, x);
  not not_1 (not_1_out, A);
  not not_2 (not_2_out, C);
  and and_1 (Dc, not_1_out, not_2_out, or_1_out, nand_1_out);
endmodule

module State_Register (
  input  Da,
  input  Db,
  input  Dc,
  input  Clock,
  output A,
  output B,
  output C
);

  D_Flip_Flop d_ff_1 (.clk(Clock), .D(Da), .Q(A));  // open: Qn, preset, en, reset
  D_Flip_Flop d_ff_2 (.clk(Clock), .D(Db), .Q(B));  // open: Qn, preset, en, reset
  D_Flip_Flop d_ff_3 (.clk(Clock), .D(Dc), .Q(C));  // open: Qn, preset, en, reset
endmodule

module Output_Combinational (
  input  A,
  input  B,
  input  C,
  output y
);

  wire not_1_out, not_2_out;

  not not_1 (not_1_out, B);
  and and_1 (y, A, not_1_out, not_2_out);
  not not_2 (not_2_out, C);
endmodule

module SSDuSS_impl (
  input  [3:0] Target,
  input  Stream,
  output Detected
);

  wire Clock_out;

  Clock Clock (.out(Clock_out));
  Sequence_Detector_using_Shift_Register Sequence_Detector (
    .Stream(Stream), .Target(Target), .Clock(Clock_out), .Detected(Detected));
  LED led_1 (.in(Detected));
endmodule

module _1_bit_Check_Match (
  input  A,
  input  Da,
  output Match
);

  wire and_1_out, and_2_out, not_1_out, not_2_out;

  not not_1 (not_1_out, A);
  not not_2 (not_2_out, Da);
  and and_1 (and_1_out, not_1_out, not_2_out);
  and and_2 (and_2_out, A, Da);
  or or_1 (Match, and_1_out, and_2_out);
endmodule

module Sequence_Detector_using_Shift_Register (
  input  Stream,
  input  [3:0] Target,
  input  Clock,
  output Detected
);

  wire _0_q, _1_q, _2_q, _3_q;

  Clock clock_1 (.out(Clock));
  D_Flip_Flop _0 (.clk(Clock), .D(Stream), .Q(_0_q));  // open: Qn, preset, en, reset
  D_Flip_Flop _1 (.clk(Clock), .D(_0_q), .Q(_1_q));  // open: Qn, preset, en, reset
  D_Flip_Flop _2 (.clk(Clock), .D(_1_q), .Q(_2_q));  // open: Qn, preset, en, reset
  D_Flip_Flop _3 (.clk(Clock), .D(_2_q), .Q(_3_q));  // open: Qn, preset, en, reset
  _4_bit_Check_Match _4_bit_Check_Match (
    .T0(Target[0]), .T1(Target[1]), .T2(Target[2]), .T3(Target[3]), .D0(_0_q), .D1(_1_q), .D2(_2_q),
    .D3(_3_q), .Match(Detected));
endmodule

module _4_bit_Check_Match (
  input  T0,
  input  T1,
  input  T2,
  input  T3,
  input  D0,
  input  D1,
  input  D2,
  input  D3,
  output Match
);

  wire n1_bit_check_match_1_match, n1_bit_check_match_2_match, n1_bit_check_match_3_match,
       n1_bit_check_match_4_match;

  _1_bit_Check_Match u_1_bit_check_match_1 (.A(T0), .Da(D0), .Match(n1_bit_check_match_1_match));
  _1_bit_Check_Match u_1_bit_check_match_2 (.A(T1), .Da(D1), .Match(n1_bit_check_match_2_match));
  _1_bit_Check_Match u_1_bit_check_match_3 (.A(T2), .Da(D2), .Match(n1_bit_check_match_3_match));
  _1_bit_Check_Match u_1_bit_check_match_4 (.A(T3), .Da(D3), .Match(n1_bit_check_match_4_match));
  and and_1 (Match, n1_bit_check_match_1_match, n1_bit_check_match_2_match, n1_bit_check_match_3_match, n1_bit_check_match_4_match);
endmodule
