// Logisim project Lab5_Ex3.circ as structural Verilog
module Sequence_Detector (
  input  x,
  input  Clock,
  output y
);

  wire Input_Combinational_ja, Input_Combinational_jb, Input_Combinational_jc, Input_Combinational_ka,
       Input_Combinational_kb, Input_Combinational_kc, State_Register_a, State_Register_b, State_Register_c;

  Input_Combinational Input_Combinational (
    .A(State_Register_a), .B(State_Register_b), .C(State_Register_c), .x(x), .Ja(Input_Combinational_ja),
    .Ka(Input_Combinational_ka), .Jb(Input_Combinational_jb), .Kb(Input_Combinational_kb),
    .Jc(Input_Combinational_jc), .Kc(Input_Combinational_kc));
  State_Register State_Register (
    .Ja(Input_Combinational_ja), .Ka(Input_Combinational_ka), .Jb(Input_Combinational_jb),
    .Kb(Input_Combinational_kb), .Jc(Input_Combinational_jc), .Kc(Input_Combinational_kc), .Clock(Clock),
    .A(State_Register_a), .B(State_Register_b), .C(State_Register_c));
  Clock clock_1 (.out(Clock));
  Output_Combinational Output_Combinational (.A(State_Register_a), .B(State_Register_b), .C(State_Register_c), .y(y));
endmodule

module Input_Combinational (
  input  A,
  input  B,
  input  C,
  input  x,
  output Ja,
  output Ka,
  output Jb,
  output Kb,
  output Jc,
  output Kc
);

  Ja u_Ja (.B(B), .C(C), .x(x), .Ja(Ja));
  Ka u_Ka (.Ka(Ka));
  Jb u_Jb (.A(A), .C(C), .x(x), .Jb(Jb));
  Kb u_Kb (.C(C), .Kb(Kb));
  Jc u_Jc (.A(A), .B(B), .x(x), .Jc(Jc));
  Kc u_Kc (.Kc(Kc));
endmodule

module Ja (
  input  B,
  input  C,
  input  x,
  output Ja
);

  and and_1 (Ja, B, C, x);
endmodule

module Ka (
  output Ka
);


  assign Ka = 1'b1;
endmodule

module Jb (
  input  A,
  input  C,
  input  x,
  output Jb
);

  wire and_1_out, and_2_out;

  and and_1 (and_1_out, A, x);
  and and_2 (and_2_out, C, x);
  or or_1 (Jb, and_1_out, and_2_out);
endmodule

module Kb (
  input  C,
  output Kb
);


  assign Kb = C;
endmodule

module Jc (
  input  A,
  input  B,
  input  x,
  output Jc
);

  wire not_1_out, not_2_out, not_3_out, or_1_out, or_2_out;

  not not_1 (not_1_out, A);
  not not_2 (not_2_out, B);
  not not_3 (not_3_out, x);
  or or_1 (or_1_out, B, x);
  or or_2 (or_2_out, not_2_out, not_3_out);
  and and_1 (Jc, not_1_out, or_1_out, or_2_out);
endmodule

module Kc (
  output Kc
);


  assign Kc = 1'b1;
endmodule

module State_Register (
  input  Ja,
  input  Ka,
  input  Jb,
  input  Kb,
  input  Jc,
  input  Kc,
  input  Clock,
  output A,
  output B,
  output C
);

  J_K_Flip_Flop j_k_ff_1 (.J(Ja), .clk(Clock), .K(Ka), .Q(A));  // open: Qn, preset, en, reset
  J_K_Flip_Flop j_k_ff_2 (.J(Jb), .clk(Clock), .K(Kb), .Q(B));  // open: Qn, preset, en, reset
  J_K_Flip_Flop j_k_ff_3 (.J(Jc), .clk(Clock), .K(Kc), .Q(C));  // open: Qn, preset, en, reset
endmodule

module Output_Combinational (
  input  A,
  input  B,
  input  C,
  output y
);

  wire not_1_out, not_2_out;

  not not_1 (not_1_out, B);
  not not_2 (not_2_out, C);
  and and_1 (y, A, not_1_out, not_2_out);
endmodule
